# Fritzing sketch CircuitBoard (saved by Fritzing 0.9.3b)
circuit board: 8.47cm x 5.64444cm
perfboards: 1

parts:
  IC1 = DIP - 16 pins [chip_label=74HC595 package="DIP (Dual Inline) [THT]"]
  J3 = male pin header, 8 pins [form="♂ (male)"]
  R5 = Resistor [tolerance=±5% resistance=10k package=THT]
  R6 = Resistor [tolerance=±5% resistance=10k package=THT]
  R3 = Resistor [tolerance=±5% resistance=10k package=THT]
  R2 = Resistor [tolerance=±5% resistance=10k package=THT]
  R1 = Resistor [tolerance=±5% resistance=10k package=THT]
  J4 = male pin header, 8 pins [form="♂ (male)"]
  IC2 = DIP - 16 pins [chip_label=74HC595 package="DIP (Dual Inline) [THT]"]
  R16 = Resistor [tolerance=±5% resistance=470 package=THT]
  J1 = male pin header, 8 pins [form="♂ (male)"]
  R7 = Resistor [tolerance=±5% resistance=10k package=THT]
  R17 = Resistor [tolerance=±5% resistance=10k package=THT]
  R18 = Resistor [tolerance=±5% resistance=10k package=THT]
  R19 = Resistor [tolerance=±5% resistance=10k package=THT]
  R20 = Resistor [tolerance=±5% resistance=10k package=THT]
  R21 = Resistor [tolerance=±5% resistance=10k package=THT]
  R22 = Resistor [tolerance=±5% resistance=10k package=THT]
  R23 = Resistor [tolerance=±5% resistance=10k package=THT]
  J2 = male pin header, 8 pins [form="♂ (male)"]
  IC4 = DIP - 16 pins [chip_label=CD4014BE package="DIP (Dual Inline) [THT]"]
  R4 = Resistor [tolerance=±5% resistance=10k package=THT]
  J5 = female pin header, 3 pins [form="♀ (female)"]
  J6 = male pin header, 6 pins [form="♂ (male)"]
  J7 = male pin header, 12 pins [form="♂ (male)"]
  Teensy = Teensy LC
  IC3 = DIP - 16 pins [chip_label=CD4014BE package="DIP (Dual Inline) [THT]"]

nets:
  N1: IC1.Q1, J3.pin8
  N2: IC1.Q2, J3.pin7
  N3: IC1.Q3, J3.pin6
  N4: IC1.Q4, J3.pin5
  N5: IC1.Q5, J3.pin4
  N6: IC1.Q6, J3.pin3
  N7: IC1.Q7, J3.pin2
  GND: IC1.GND, IC1.OE, IC2.GND, IC2.OE, J1.pin1, J2.pin1, IC4.GND, J5.pin1, Teensy.GND#27, IC3.GND
  N8: IC1.Q7', IC2.DS
  5V: IC1.MR, IC1.Vcc, R5.Pin_0, R6.Pin_0, R3.Pin_0, R2.Pin_0, R1.Pin_0, IC2.MR, IC2.Vcc, R16.Pin_0, R7.Pin_0, R17.Pin_0, R18.Pin_0, R19.Pin_0, R20.Pin_0, R21.Pin_0, R22.Pin_0, R23.Pin_0, IC4.Vcc, R4.Pin_0, J5.pin3, J7.pin12, Teensy.3.3V, IC3.Vcc
  N9: IC1.SH_CP, IC2.SH_CP, J6.pin5, Teensy.17_/_A3
  N10: IC1.ST_CP, IC2.ST_CP, J6.pin6, Teensy.18_/_A4
  N11: IC1.DS, J6.pin4, Teensy.16_/_A2
  N12: J3.pin1, J4.pin1, R16.Pin_1
  N13: R5.Pin_1, J1.pin4, IC3.PI-3
  N14: R6.Pin_1, J1.pin3, IC3.PI-2
  N15: R3.Pin_1, J1.pin6, IC3.PI-5
  N16: R2.Pin_1, J1.pin7, IC3.PI-6
  N17: R1.Pin_1, J1.pin8, IC3.PI-7
  N18: J4.pin2, IC2.Q7
  N19: J4.pin3, IC2.Q6
  N20: J4.pin4, IC2.Q5
  N21: J4.pin5, IC2.Q4
  N22: J4.pin6, IC2.Q3
  N23: J4.pin7, IC2.Q2
  N24: J4.pin8, IC2.Q1
  N25: J1.pin2, R7.Pin_1, IC3.PI-1
  N26: J1.pin5, R4.Pin_1, IC3.PI-4
  N27: R17.Pin_1, J2.pin8, IC4.PI-7, J7.pin11
  N28: R18.Pin_1, J2.pin7, IC4.PI-6
  N29: R19.Pin_1, J2.pin6, IC4.PI-5
  N30: R20.Pin_1, J2.pin2, IC4.PI-1
  N31: R21.Pin_1, J2.pin3, IC4.PI-2
  N32: R22.Pin_1, J2.pin4, IC4.PI-3
  N33: R23.Pin_1, J2.pin5, IC4.PI-4
  N34: IC4.Q8, IC3.Ser-In
  N35: IC4.P/S-Ctrl, J6.pin3, Teensy.15_/_A1, IC3.P/S-Ctrl
  N36: IC4.CLK, J6.pin2, Teensy.14_/_A0, IC3.CLK
  N37: J5.pin2, Teensy.19_/_A5
  N38: J6.pin1, Teensy.13_/_(LED), IC3.Q8
  N39: J7.pin1, Teensy.12
  N40: J7.pin2, Teensy.11
  N41: J7.pin3, Teensy.10_/_TX2
  N42: J7.pin4, Teensy.9_/_RX2
  N43: J7.pin5, Teensy.8_/_TX3
  N44: J7.pin6, Teensy.7_/_RX3
  N45: J7.pin7, Teensy.6_/_(RX3)
  N46: J7.pin8, Teensy.5_/_(TX1)
  N47: J7.pin9, Teensy.4_/_(TX1)
  N48: J7.pin10, Teensy.3_/_(RX1)

custom parts:
  DIP - 16 pins: A DIP stand-in part for whatever IC you want. With 16 pins on a 300mil dual inline package (DIP) footprint.
  DIP - 16 pins: A DIP stand-in part for whatever IC you want. With 16 pins on a 300mil dual inline package (DIP) footprint.
  Teensy LC: Teensy-LC delivers an impressive collection of capabilities to make modern electronic projects simpler. It features an ARM Cortex-M0+ processor at 48 MHz, 62K Flash, 8K RAM, 12 bit analog input & output, hardware Serial, SPI & I2C, USB, and a total of 27 I/O pins.
